# Fritzing sketch attiny85_pov (saved by Fritzing 0.9.3b)
breadboards: 1

parts:
  U1 = attiny85 [package=dip]
  part = smd LED [color="Red (633nm)" package="1206 [SMD]"]
  part_2 = smd LED [color="Red (633nm)" package="1206 [SMD]"]
  part_3 = smd LED [color="Red (633nm)" package="1206 [SMD]"]
  part_4 = smd LED [color="Red (633nm)" package="1206 [SMD]"]
  part_5 = smd LED [color="Red (633nm)" package="1206 [SMD]"]

nets:
  N1: U1.Pin_2, part_4.anode
  N2: U1.Pin_3, part_5.anode
  N3: U1.Pin_4, part.cathode, part_2.cathode, part_3.cathode, part_4.cathode, part_5.cathode
  N4: U1.Pin_5, part.anode
  N5: U1.Pin_6, part_2.anode
  N6: U1.Pin_7, part_3.anode
